# Fritzing sketch 16-port (saved by Fritzing 0.9.3b)
perfboards: 1

parts:
  HCF_1 = HCF 4067 [package="DIP24 [THT]"]
  U7 = 74HC595 [package="DIP16 [THT]"]
  U8 = 74HC595 [package="DIP16 [THT]"]
  R1 = Resistor [tolerance=±5% resistance=220 package=THT]
  R2 = Resistor [tolerance=±5% resistance=220 package=THT]
  R3 = Resistor [tolerance=±5% resistance=220 package=THT]
  R4 = Resistor [tolerance=±5% resistance=220 package=THT]
  R5 = Resistor [tolerance=±5% resistance=220 package=THT]
  R6 = Resistor [tolerance=±5% resistance=220 package=THT]
  R7 = Resistor [tolerance=±5% resistance=220 package=THT]
  R8 = Resistor [tolerance=±5% resistance=220 package=THT]
  R9 = Resistor [tolerance=±5% resistance=220 package=THT]
  R10 = Resistor [tolerance=±5% resistance=220 package=THT]
  R11 = Resistor [tolerance=±5% resistance=220 package=THT]
  R12 = Resistor [tolerance=±5% resistance=220 package=THT]
  R13 = Resistor [tolerance=±5% resistance=220 package=THT]
  R14 = Resistor [tolerance=±5% resistance=220 package=THT]
  R15 = Resistor [tolerance=±5% resistance=220 package=THT]
  R16 = Resistor [tolerance=±5% resistance=220 package=THT]
  Part2 = Arduino Pro Mini v13
  J1 = double row female pin header, 16 pins [form="♀ (female)"]
  J2 = double row female pin header, 16 pins [form="♀ (female)"]
  J3 = double row female pin header, 16 pins [form="♀ (female)"]  # not connected
  R17 = Resistor [tolerance=±5% resistance=10k package=THT]
  HCF_2 = HCF 4067 [package="DIP24 [THT]"]
  J4 = Power Jack [package=power_jack_pth_lock]

nets:
  N1: HCF_1.1_O/I, R17.Pin_0
  N2: HCF_1.2_TG_7, HCF_2.2_TG_7
  N3: HCF_1.3_TG6, HCF_2.3_TG6
  N4: HCF_1.4_TG5, HCF_2.4_TG5
  N5: HCF_1.5_TG4, HCF_2.5_TG4
  N6: HCF_1.6_TG3, HCF_2.6_TG3
  N7: HCF_1.7_TG2, HCF_2.7_TG2
  N8: HCF_1.8_TG1, HCF_2.8_TG1
  N9: HCF_1.9_TG0, HCF_2.9_TG0
  N10: HCF_1.10_A, Part2.D3_PWM
  N11: HCF_1.11_B, Part2.D2
  GND: HCF_1.12_VSS, HCF_1.15_Inhibit, U7.GND, U7.OE, U8.GND, U8.OE, Part2.GND, J2.pin1, J2.pin2, J2.pin3, J2.pin4, J2.pin5, J2.pin6, J2.pin7, J2.pin8, J2.pin9, J2.pin10, J2.pin11, J2.pin12, J2.pin13, J2.pin14, J2.pin15, J2.pin16, HCF_2.12_VSS, HCF_2.15_Inhibit, J4.GND
  N12: HCF_1.13_D, Part2.D4
  N13: HCF_1.14_C, Part2.D5_PWM
  N14: HCF_1.16_TG15, HCF_2.16_TG15
  N15: HCF_1.17_TG14, HCF_2.17_TG14
  N16: HCF_1.18_TG13, HCF_2.18_TG13
  N17: HCF_1.19_TG12, HCF_2.19_TG12
  N18: HCF_1.20_TG11, HCF_2.20_TG11
  N19: HCF_1.21_TG10, HCF_2.21_TG10
  N20: HCF_1.22_TG9, HCF_2.22_TG9
  N21: HCF_1.23_TG8, HCF_2.23_TG8
  VCC: HCF_1.24_Vdd, U7.VCC, Part2.VCC, HCF_2.24_Vdd, J4.PWR
  N22: U7.Q1, R15.Pin_0
  N23: U7.Q2, R14.Pin_0
  N24: U7.Q3, R13.Pin_0
  N25: U7.Q4, R12.Pin_0
  N26: U7.Q5, R11.Pin_0
  N27: U7.Q6, R10.Pin_0
  N28: U7.Q7, R9.Pin_0
  N29: U7.Q7', U8.DS
  N30: U7.SH_CP, U8.SH_CP, Part2.D11_PWM/MOSI
  N31: U7.ST_CP, U8.ST_CP, Part2.D10_PWM/SS
  N32: U7.DS, Part2.D12/MISO
  N33: U7.Q0, R1.Pin_0
  N34: U8.Q1, R7.Pin_0
  N35: U8.Q2, R6.Pin_0
  N36: U8.Q3, R5.Pin_0
  N37: U8.Q4, R4.Pin_0
  N38: U8.Q5, R3.Pin_0
  N39: U8.Q6, R2.Pin_0
  N40: U8.Q7, R16.Pin_0
  N41: U8.Q0, R8.Pin_0
  N42: R1.Pin_1, J1.pin1
  N43: R2.Pin_1, J1.pin15
  N44: R3.Pin_1, J1.pin14
  N45: R4.Pin_1, J1.pin13
  N46: R5.Pin_1, J1.pin12
  N47: R6.Pin_1, J1.pin11
  N48: R7.Pin_1, J1.pin10
  N49: R8.Pin_1, J1.pin9
  N50: R9.Pin_1, J1.pin8
  N51: R10.Pin_1, J1.pin7
  N52: R11.Pin_1, J1.pin6
  N53: R12.Pin_1, J1.pin5
  N54: R13.Pin_1, J1.pin4
  N55: R14.Pin_1, J1.pin3
  N56: R15.Pin_1, J1.pin2
  N57: R16.Pin_1, J1.pin16
  N58: Part2.A0, HCF_2.1_O/I
  N59: Part2.D13/SCK, R17.Pin_1
  N60: Part2.D9_PWM, HCF_2.14_C
  N61: Part2.D8, HCF_2.13_D
  N62: Part2.D7, HCF_2.10_A
  N63: Part2.D6_PWM, HCF_2.11_B
